# Fritzing sketch hello_lcd (saved by Fritzing 0.9.3b)
breadboards: 1

parts:
  U1 = LCD-16X2 [package=lcd-16x2]  # not connected
  R1 = Rotary Potentiometer (Small) [maximum_resistance=100kΩ package=THT]
  Part1 = Arduino Uno (Rev3)

nets:
  N1: R1.leg1, Part1.5V
  N2: R1.leg2, Part1.GND
