# Fritzing sketch motor_control (saved by Fritzing 0.9.3b)
breadboards: 1

parts:
  Part1 = Arduino Uno (Rev3)
  D1 = Diode [package=diode-1n4148]
  Q1 = NPN-Transistor [package="SOT-23 [SMD]"]
  R1 = Resistor [tolerance=±5% resistance=220 package=THT]
  U1 = POT [package=3362u]
  VCC1 = 4 x AAA Battery Mount
  M1 = DC Motor

nets:
  N1: Part1.A0, U1.S
  N2: Part1.D11_PWM/MOSI, R1.Pin_0
  N3: Part1.5V, U1.A
  N4: Part1.GND, Q1.2, U1.E, VCC1.-
  N5: D1.C, VCC1.+, M1.pin_2
  N6: Q1.0, R1.Pin_1
  N7: Q1.1, M1.pin_1
