# Fritzing sketch photointerruptor (saved by Fritzing 0.9.3b)
breadboards: 1

parts:
  Part1 = Arduino Uno (Rev3)
  Q1 = PHOTOTRANSISTOR REFLECTIVE OBJECT SENSOR [package=qrb1114-side]
  LED2 = smd LED [color="Red (633nm)" package="0603 [SMD]"]

nets:
  N1: Part1.GND, Q1.A, Q1.E, Q1.K, LED2.cathode
  N2: Part1.D2, Part1.D3_PWM, Q1.C
  N3: Part1.D7, LED2.anode
