# Fritzing sketch PID_Rough_Draft (saved by Fritzing 0.9.3b)
breadboards: 3

parts:
  Part1 = Arduino Uno (Rev3)
  Q1 = PHOTOTRANSISTOR REFLECTIVE OBJECT SENSOR [package=qrb1114-side]
  Q2 = NPN-Transistor [package="SOT-23 [SMD]"]
  R2 = Resistor [tolerance=±5% resistance=220 package=THT]
  R3 = Rotary Potentiometer (Small) [maximum_resistance=100kΩ package=THT]
  VCC3 = Battery
  VCC5 = Battery
  START_2 = Toggle Switch [package=THT]
  Adjust_Brightness_++_-- = Pushbutton [package="[THT]"]
  S3 = Pushbutton [package="[THT]"]
  LED2 = LED - 5mm [color="Red (633nm)" package="5 mm [THT]"]  # not connected
  SELECT_4 = Toggle Switch [package=THT]
  Q3 = NPN-Transistor [package="SOT-23 [SMD]"]
  LCD2 = LCD screen
  LCM1602_IIC2 = LCM1602 IIC [part_number="LCM1602 IIC" chip_label="LCM1602 IIC" package="DIP (Dual Inline) [THT]"]
  R4 = Resistor [tolerance=±5% resistance=10k package=THT]
  R5 = Resistor [tolerance=±5% resistance=10k package=THT]
  R6 = Resistor [tolerance=±5% resistance=10k package=THT]
  R7 = Resistor [tolerance=±5% resistance=10k package=THT]
  R8 = Resistor [tolerance=±5% resistance=220 package=THT]
  M1 = DC Motor
  D1 = Rectifier Diode [part_number=1N4001 package="300 mil [THT]"]

nets:
  N1: Part1.A4/SDA, LCM1602_IIC2.SDA
  N2: Part1.A5/SCL, LCM1602_IIC2.SCL
  N3: Part1.D8, SELECT_4.L1, R5.Pin_0
  5V: Part1.D11_PWM/MOSI, Part1.D12/MISO, Part1.5V, R3.leg1, START_2.COM, Adjust_Brightness_++_--.Pin_3, Adjust_Brightness_++_--.Pin_4, S3.Pin_3, S3.Pin_4, SELECT_4.COM, LCM1602_IIC2.VCC, R6.Pin_0, R7.Pin_0
  GND: Part1.GND, VCC5.-, LCM1602_IIC2.GND, R4.Pin_1
  N4: Part1.D5_PWM, R8.Pin_1
  N5: Part1.D7, START_2.L1, R4.Pin_0
  N6: Q1.A, Q1.K
  N7: Q1.E, Q2.1
  N8: Q2.0, R2.Pin_1
  N9: VCC3.+, M1.pin_2, D1.cathode
  N10: Adjust_Brightness_++_--.Pin_1, Adjust_Brightness_++_--.Pin_2
  N11: S3.Pin_1, S3.Pin_2
  N12: Q3.2, M1.pin_1, D1.anode
  N13: Q3.0, R8.Pin_0
  VSS: LCD2.VSS, LCM1602_IIC2.VSS
  VDD: LCD2.VDD, LCM1602_IIC2.VDD
  N14: LCD2.V0, LCM1602_IIC2.V0
  N15: LCD2.RS, LCM1602_IIC2.RS
  N16: LCD2.R/W, LCM1602_IIC2.RW
  N17: LCD2.E, LCM1602_IIC2.E
  N18: LCD2.DB0, LCM1602_IIC2.D0
  N19: LCD2.DB1, LCM1602_IIC2.D1
  N20: LCD2.DB2, LCM1602_IIC2.D2
  N21: LCD2.DB3, LCM1602_IIC2.D3
  N22: LCD2.DB4, LCM1602_IIC2.D4
  N23: LCD2.DB5, LCM1602_IIC2.D5
  N24: LCD2.DB6, LCM1602_IIC2.D6
  N25: LCD2.DB7, LCM1602_IIC2.D7
  N26: LCD2.LED+, LCM1602_IIC2.A
  N27: LCD2.LED-, LCM1602_IIC2.K
  N28: LCM1602_IIC2.LED_A, LCM1602_IIC2.LED_B

custom parts:
  LCM1602 IIC: I2C-Module to use a 1602 or 2004 LCD on with the wire.h libory Serial LCD Modul
