# Fritzing sketch PID_Rough_Draft_Power_Port_up (saved by Fritzing 0.9.3b)
breadboards: 3

parts:
  Q1 = PHOTOTRANSISTOR REFLECTIVE OBJECT SENSOR [package=qrb1114-side]
  Q2 = NPN-Transistor [package="SOT-23 [SMD]"]
  R2 = Resistor [tolerance=±5% resistance=220 package=THT]
  M2 = DC Motor
  R3 = Rotary Potentiometer (Small) [maximum_resistance=100kΩ package=THT]
  VCC3 = Battery  # not connected
  VCC5 = Battery
  START_2 = Toggle Switch [package=THT]
  LED1 = LED - 5mm [color="Red (633nm)" package="5 mm [THT]"]  # not connected
  Adjust_Brightness_++_-- = Pushbutton [package="[THT]"]
  S3 = Pushbutton [package="[THT]"]
  LED2 = LED - 5mm [color="Red (633nm)" package="5 mm [THT]"]  # not connected
  SELECT_4 = Toggle Switch [package=THT]
  Q3 = NPN-Transistor [package="SOT-23 [SMD]"]
  LCD2 = LCD screen
  LCM1602_IIC2 = LCM1602 IIC [part_number="LCM1602 IIC" chip_label="LCM1602 IIC" package="DIP (Dual Inline) [THT]"]
  Part2 = Arduino Uno (Rev3)
  R5 = Resistor [tolerance=±5% resistance=10k package=THT]
  R6 = Resistor [tolerance=±5% resistance=10k package=THT]
  R7 = Resistor [tolerance=±5% resistance=10k package=THT]
  R8 = Resistor [tolerance=±5% resistance=10k package=THT]
  R9 = Resistor [tolerance=±5% resistance=220 package=THT]
  D2 = Rectifier Diode [part_number=1N4001 package="300 mil [THT]"]

nets:
  N1: Q1.A, Q1.K
  N2: Q1.E, Q2.1
  N3: Q2.0, R2.Pin_1
  N4: M2.pin_1, Q3.2, D2.anode
  N5: M2.pin_2, D2.cathode
  VCC: R3.leg1, START_2.COM, Adjust_Brightness_++_--.Pin_3, Adjust_Brightness_++_--.Pin_4, S3.Pin_3, S3.Pin_4, SELECT_4.COM, LCM1602_IIC2.VCC, Part2.D8, Part2.D7, Part2.5V, R7.Pin_0, R8.Pin_0
  N6: R3.wiper, Part2.A0
  GND: R3.leg2, VCC5.-, Q3.1, LCM1602_IIC2.GND, Part2.GND, R5.Pin_1, R6.Pin_1, R7.Pin_1, R8.Pin_1
  N7: START_2.L1, Part2.D5_PWM, R5.Pin_0
  N8: Adjust_Brightness_++_--.Pin_1, Adjust_Brightness_++_--.Pin_2
  N9: S3.Pin_1, S3.Pin_2
  N10: SELECT_4.L1, Part2.D6_PWM, R6.Pin_0
  N11: Q3.0, R9.Pin_0
  VSS: LCD2.VSS, LCM1602_IIC2.VSS
  VDD: LCD2.VDD, LCM1602_IIC2.VDD
  N12: LCD2.V0, LCM1602_IIC2.V0
  N13: LCD2.RS, LCM1602_IIC2.RS
  N14: LCD2.R/W, LCM1602_IIC2.RW
  N15: LCD2.E, LCM1602_IIC2.E
  N16: LCD2.DB0, LCM1602_IIC2.D0
  N17: LCD2.DB1, LCM1602_IIC2.D1
  N18: LCD2.DB2, LCM1602_IIC2.D2
  N19: LCD2.DB3, LCM1602_IIC2.D3
  N20: LCD2.DB4, LCM1602_IIC2.D4
  N21: LCD2.DB5, LCM1602_IIC2.D5
  N22: LCD2.DB6, LCM1602_IIC2.D6
  N23: LCD2.DB7, LCM1602_IIC2.D7
  N24: LCD2.LED+, LCM1602_IIC2.A
  N25: LCD2.LED-, LCM1602_IIC2.K
  N26: LCM1602_IIC2.SDA, Part2.A4/SDA
  N27: LCM1602_IIC2.SCL, Part2.A5/SCL
  N28: LCM1602_IIC2.LED_A, LCM1602_IIC2.LED_B
  N29: Part2.D11_PWM/MOSI, R9.Pin_1

custom parts:
  LCM1602 IIC: I2C-Module to use a 1602 or 2004 LCD on with the wire.h libory Serial LCD Modul
